// Logisim project control_logic.circ as structural Verilog: 1 circuit, main circuit control_logic
module control_logic (
  input  [31:0] inst,
  input  BrEq,
  input  BrLt,
  output PCSel,
  output RegWEn,
  output [2:0] ImmSel,
  output BrUn,
  output ASel,
  output BSel,
  output [3:0] ALUSel,
  output MemRW,
  output [1:0] WBSel,
  output CSRSel,
  output CSRWen
);

  wire and_1_out, and_2_out, and_3_out, and_31_out, and_32_out, and_33_out, and_34_out, and_35_out,
       and_36_out, comparator_1_eq, comparator_2_eq, comparator_3_eq, comparator_4_eq, comparator_5_eq,
       comparator_6_eq, comparator_7_eq, comparator_8_eq, comparator_9_eq, comparator_10_eq,
       comparator_19_lt, comparator_21_eq, comparator_22_eq, comparator_23_eq, comparator_24_eq,
       comparator_25_eq, comparator_26_eq, comparator_27_eq, comparator_28_eq, comparator_29_eq,
       comparator_30_eq, comparator_31_eq, comparator_32_eq, comparator_33_eq, comparator_34_eq,
       comparator_35_eq, comparator_36_eq, comparator_37_eq, comparator_38_eq, comparator_39_eq,
       comparator_40_eq, is_add, is_add_addi, is_addi, is_and, is_and_andi, is_andi, is_auipc, is_B,
       is_B_true, is_beq, is_bge, is_bgeu, is_blt, is_bltu, is_bne, is_csrw, is_I_imm, is_I_load, is_jal,
       is_jalr, is_lui, is_mul, is_mulh, is_mulhu, is_or, is_or_ori, is_ori, is_R, is_sll, is_sll_slli,
       is_slli, is_slt, is_slt_slti, is_slti, is_sra, is_sra_srai, is_srai, is_srl, is_srl_srli, is_srli,
       is_sub, is_xor, is_xor_xori, is_xori, nor_1_out, not_2_out, not_3_out, not_4_out, or_2_out, or_3_out,
       or_4_out, or_12_out, or_19_out, or_20_out;
  wire [1:0] multiplexer_20_out, multiplexer_21_out;
  wire [2:0] multiplexer_1_out, multiplexer_2_out, multiplexer_3_out, multiplexer_4_out, multiplexer_5_out;
  wire [3:0] bit_extender_1_out, multiplexer_6_out, multiplexer_7_out, multiplexer_8_out, multiplexer_9_out,
       multiplexer_10_out, multiplexer_11_out, multiplexer_12_out, multiplexer_13_out, multiplexer_14_out,
       multiplexer_15_out, multiplexer_16_out, multiplexer_17_out, multiplexer_18_out, multiplexer_19_out,
       R_I_ALUSel;
  wire [7:0] bit_extender_2_out;

  assign bit_extender_1_out = {{1{1'b0}}, inst[14:12]};  // Bit_Extender bit_extender_1
  assign bit_extender_2_out = {{1{1'b0}}, inst[31:25]};  // Bit_Extender bit_extender_2
  or or_1 (PCSel, is_jalr, is_B_true, is_jal);
  or or_2 (or_2_out, is_I_load, is_I_imm, is_jalr);
  or or_3 (or_3_out, is_lui, is_auipc);
  Comparator #(.mode("unsigned"), .width(4)) comparator_1 (
    .a(bit_extender_1_out), .b(4'b0000), .eq(comparator_1_eq));  // open: gt, lt
  Comparator #(.mode("unsigned"), .width(4)) comparator_2 (
    .a(bit_extender_1_out), .b(4'b0001), .eq(comparator_2_eq));  // open: gt, lt
  Comparator #(.mode("unsigned")) comparator_3 (
    .a(bit_extender_2_out), .b({8{1'b0}}), .eq(comparator_3_eq));  // open: gt, lt
  Comparator #(.mode("unsigned"), .width(4)) comparator_4 (
    .a(bit_extender_1_out), .b(4'b0010), .eq(comparator_4_eq));  // open: gt, lt
  Comparator #(.mode("unsigned"), .width(4)) comparator_5 (
    .a(bit_extender_1_out), .b(4'b0100), .eq(comparator_5_eq));  // open: gt, lt
  Comparator #(.mode("unsigned"), .width(4)) comparator_6 (
    .a(bit_extender_1_out), .b(4'b0101), .eq(comparator_6_eq));  // open: gt, lt
  Comparator #(.mode("unsigned")) comparator_7 (
    .a(bit_extender_2_out), .b({8{1'b0}}), .eq(comparator_7_eq));  // open: gt, lt
  Comparator #(.mode("unsigned")) comparator_8 (
    .a(bit_extender_2_out), .b(8'h20), .eq(comparator_8_eq));  // open: gt, lt
  Comparator #(.mode("unsigned"), .width(4)) comparator_9 (
    .a(bit_extender_1_out), .b(4'b0110), .eq(comparator_9_eq));  // open: gt, lt
  Comparator #(.mode("unsigned"), .width(4)) comparator_10 (
    .a(bit_extender_1_out), .b(4'b0111), .eq(comparator_10_eq));  // open: gt, lt
  Comparator #(.width(7)) comparator_11 (.a(inst[6:0]), .b(7'b0110011), .eq(is_R));  // open: gt, lt
  Comparator #(.width(7)) comparator_12 (.a(inst[6:0]), .b(7'b0000011), .eq(is_I_load));  // open: gt, lt
  Comparator #(.width(7)) comparator_13 (.a(inst[6:0]), .b(7'b0010011), .eq(is_I_imm));  // open: gt, lt
  Comparator #(.width(7)) comparator_14 (.a(inst[6:0]), .b(7'b0100011), .eq(MemRW));  // open: gt, lt
  Comparator #(.width(7)) comparator_15 (.a(inst[6:0]), .b(7'b1100011), .eq(is_B));  // open: gt, lt
  Comparator #(.width(7)) comparator_16 (.a(inst[6:0]), .b(7'b0010111), .eq(is_auipc));  // open: gt, lt
  Comparator #(.width(7)) comparator_17 (.a(inst[6:0]), .b(7'b0110111), .eq(is_lui));  // open: gt, lt
  Comparator #(.width(7)) comparator_18 (.a(inst[6:0]), .b(7'b1101111), .eq(is_jal));  // open: gt, lt
  Comparator #(.width(7)) comparator_19 (
    .a(inst[6:0]), .b(7'b1100111), .eq(is_jalr), .lt(comparator_19_lt));  // open: gt
  Comparator #(.width(7)) comparator_20 (.a(inst[6:0]), .b(7'b1110011), .eq(CSRWen));  // open: gt, lt
  Multiplexer #(.enable("false"), .width(3)) multiplexer_1 (
    .in0(3'b000), .in1(3'b000), .out(multiplexer_1_out), .sel(or_2_out));
  Multiplexer #(.enable("false"), .width(3)) multiplexer_2 (
    .in0(3'b000), .in1(3'b001), .out(multiplexer_2_out), .sel(MemRW));
  Multiplexer #(.enable("false"), .width(3)) multiplexer_3 (
    .in0(3'b000), .in1(3'b100), .out(multiplexer_3_out), .sel(is_jal));
  Multiplexer #(.enable("false"), .width(3)) multiplexer_4 (
    .in0(3'b000), .in1(3'b011), .out(multiplexer_4_out), .sel(or_3_out));
  Multiplexer #(.enable("false"), .width(3)) multiplexer_5 (
    .in0(3'b000), .in1(3'b010), .out(multiplexer_5_out), .sel(is_B));
  nor nor_1 (nor_1_out, is_blt, is_bge);
  or or_4 (or_4_out, is_bltu, is_bgeu);
  and and_1 (and_1_out, comparator_2_eq, comparator_3_eq);
  and and_2 (and_2_out, comparator_6_eq, comparator_7_eq);
  and and_3 (and_3_out, comparator_6_eq, comparator_8_eq);
  Comparator #(.mode("unsigned"), .width(3)) comparator_21 (
    .a(inst[14:12]), .b(3'b000), .eq(comparator_21_eq));  // open: gt, lt
  Comparator #(.mode("unsigned"), .width(3)) comparator_22 (
    .a(inst[14:12]), .b(3'b001), .eq(comparator_22_eq));  // open: gt, lt
  Comparator #(.mode("unsigned"), .width(3)) comparator_23 (
    .a(inst[14:12]), .b(3'b100), .eq(comparator_23_eq));  // open: gt, lt
  Comparator #(.mode("unsigned"), .width(3)) comparator_24 (
    .a(inst[14:12]), .b(3'b101), .eq(comparator_24_eq));  // open: gt, lt
  Comparator #(.mode("unsigned"), .width(3)) comparator_25 (
    .a(inst[14:12]), .b(3'b110), .eq(comparator_25_eq));  // open: gt, lt
  Comparator #(.mode("unsigned"), .width(3)) comparator_26 (
    .a(inst[14:12]), .b(3'b111), .eq(comparator_26_eq));  // open: gt, lt
  assign ImmSel = multiplexer_1_out | multiplexer_2_out | multiplexer_3_out | multiplexer_4_out | multiplexer_5_out;  // OR_Gate or_5, 3 bits wide
  and and_4 (is_beq, comparator_21_eq, is_B);
  and and_5 (is_bne, comparator_22_eq, is_B);
  and and_6 (is_blt, comparator_23_eq, is_B);
  and and_7 (is_bge, comparator_24_eq, is_B);
  and and_8 (is_bltu, comparator_25_eq, is_B);
  and and_9 (is_bgeu, comparator_26_eq, is_B);
  and and_10 (BrUn, nor_1_out, or_4_out);
  and and_11 (is_addi, comparator_1_eq, is_I_imm);
  and and_12 (is_slli, and_1_out, is_I_imm);
  and and_13 (is_slti, comparator_4_eq, is_I_imm);
  and and_14 (is_xori, comparator_5_eq, is_I_imm);
  and and_15 (is_srli, and_2_out, is_I_imm);
  and and_16 (is_srai, and_3_out, is_I_imm);
  and and_17 (is_ori, comparator_9_eq, is_I_imm);
  and and_18 (is_andi, comparator_10_eq, is_I_imm);
  Comparator #(.mode("unsigned"), .width(12)) comparator_27 (
    .a({1'b0, inst[14:12], 1'b0, inst[31:25]}), .b({12{1'b0}}), .eq(comparator_27_eq));  // open: gt, lt
  Comparator #(.mode("unsigned"), .width(12)) comparator_28 (
    .a({1'b0, inst[14:12], 1'b0, inst[31:25]}), .b(12'h1), .eq(comparator_28_eq));  // open: gt, lt
  Comparator #(.mode("unsigned"), .width(12)) comparator_29 (
    .a({1'b0, inst[14:12], 1'b0, inst[31:25]}), .b(12'h20), .eq(comparator_29_eq));  // open: gt, lt
  Comparator #(.mode("unsigned"), .width(12)) comparator_30 (
    .a({1'b0, inst[14:12], 1'b0, inst[31:25]}), .b(12'h100), .eq(comparator_30_eq));  // open: gt, lt
  Comparator #(.mode("unsigned"), .width(12)) comparator_31 (
    .a({1'b0, inst[14:12], 1'b0, inst[31:25]}), .b(12'h101), .eq(comparator_31_eq));  // open: gt, lt
  Comparator #(.mode("unsigned"), .width(12)) comparator_32 (
    .a({1'b0, inst[14:12], 1'b0, inst[31:25]}), .b(12'h301), .eq(comparator_32_eq));  // open: gt, lt
  Comparator #(.mode("unsigned"), .width(12)) comparator_33 (
    .a({1'b0, inst[14:12], 1'b0, inst[31:25]}), .b(12'h200), .eq(comparator_33_eq));  // open: gt, lt
  Comparator #(.mode("unsigned"), .width(12)) comparator_34 (
    .a({1'b0, inst[14:12], 1'b0, inst[31:25]}), .b(12'h400), .eq(comparator_34_eq));  // open: gt, lt
  Comparator #(.mode("unsigned"), .width(12)) comparator_35 (
    .a({1'b0, inst[14:12], 1'b0, inst[31:25]}), .b(12'h500), .eq(comparator_35_eq));  // open: gt, lt
  Comparator #(.mode("unsigned"), .width(12)) comparator_36 (
    .a({1'b0, inst[14:12], 1'b0, inst[31:25]}), .b(12'h520), .eq(comparator_36_eq));  // open: gt, lt
  Comparator #(.mode("unsigned"), .width(12)) comparator_37 (
    .a({1'b0, inst[14:12], 1'b0, inst[31:25]}), .b(12'h600), .eq(comparator_37_eq));  // open: gt, lt
  Comparator #(.mode("unsigned"), .width(12)) comparator_38 (
    .a({1'b0, inst[14:12], 1'b0, inst[31:25]}), .b(12'h700), .eq(comparator_38_eq));  // open: gt, lt
  nor nor_2 (RegWEn, CSRWen, MemRW, is_B);
  not not_1 (BSel, is_R);
  or or_6 (ASel, is_jal, is_B, is_auipc);
  not not_2 (not_2_out, BrEq);
  not not_3 (not_3_out, BrLt);
  not not_4 (not_4_out, BrLt);
  and and_19 (is_add, comparator_27_eq, is_R);
  and and_20 (is_mul, comparator_28_eq, is_R);
  and and_21 (is_sub, comparator_29_eq, is_R);
  and and_22 (is_sll, comparator_30_eq, is_R);
  and and_23 (is_mulh, comparator_31_eq, is_R);
  and and_24 (is_mulhu, comparator_32_eq, is_R);
  and and_25 (is_slt, comparator_33_eq, is_R);
  and and_26 (is_xor, comparator_34_eq, is_R);
  and and_27 (is_srl, comparator_35_eq, is_R);
  and and_28 (is_sra, comparator_36_eq, is_R);
  and and_29 (is_or, comparator_37_eq, is_R);
  and and_30 (is_and, comparator_38_eq, is_R);
  or or_7 (is_add_addi, is_add, is_addi);
  or or_8 (is_sll_slli, is_sll, is_slli);
  or or_9 (is_slt_slti, is_slt, is_slti);
  or or_10 (is_xor_xori, is_xor, is_xori);
  and and_31 (and_31_out, is_beq, BrEq);
  and and_32 (and_32_out, is_bne, not_2_out);
  and and_33 (and_33_out, is_blt, BrLt);
  and and_34 (and_34_out, is_bge, not_3_out);
  and and_35 (and_35_out, is_bltu, BrLt);
  and and_36 (and_36_out, is_bgeu, not_4_out);
  or or_11 (is_B_true, and_31_out, and_32_out, and_33_out, and_34_out, and_35_out, and_36_out);
  or or_12 (or_12_out, is_R, is_I_imm);
  Multiplexer #(.enable("false"), .width(4)) multiplexer_6 (
    .in0(4'b0000), .in1(4'b0000), .out(multiplexer_6_out), .sel(is_add_addi));
  Multiplexer #(.enable("false"), .width(4)) multiplexer_7 (
    .in0(4'b0000), .in1(4'b1010), .out(multiplexer_7_out), .sel(is_mul));
  Multiplexer #(.enable("false"), .width(4)) multiplexer_8 (
    .in0(4'b0000), .in1(4'b1100), .out(multiplexer_8_out), .sel(is_sub));
  Multiplexer #(.enable("false"), .width(4)) multiplexer_9 (
    .in0(4'b0000), .in1(4'b0110), .out(multiplexer_9_out), .sel(is_sll_slli));
  Multiplexer #(.enable("false"), .width(4)) multiplexer_10 (
    .in0(4'b0000), .in1(4'b1110), .out(multiplexer_10_out), .sel(is_mulh));
  Multiplexer #(.enable("false"), .width(4)) multiplexer_11 (
    .in0(4'b0000), .in1(4'b1011), .out(multiplexer_11_out), .sel(is_mulhu));
  Multiplexer #(.enable("false"), .width(4)) multiplexer_12 (
    .in0(4'b0000), .in1(4'b0111), .out(multiplexer_12_out), .sel(is_slt_slti));
  Multiplexer #(.enable("false"), .width(4)) multiplexer_13 (
    .in0(4'b0000), .in1(4'b0011), .out(multiplexer_13_out), .sel(is_xor_xori));
  Multiplexer #(.enable("false"), .width(4)) multiplexer_14 (
    .in0(4'b0000), .in1(4'b0100), .out(multiplexer_14_out), .sel(is_srl_srli));
  Multiplexer #(.enable("false"), .width(4)) multiplexer_15 (
    .in0(4'b0000), .in1(4'b0101), .out(multiplexer_15_out), .sel(is_sra_srai));
  Multiplexer #(.enable("false"), .width(4)) multiplexer_16 (
    .in0(4'b0000), .in1(4'b0010), .out(multiplexer_16_out), .sel(is_or_ori));
  Multiplexer #(.enable("false"), .width(4)) multiplexer_17 (
    .in0(4'b0000), .in1(4'b0001), .out(multiplexer_17_out), .sel(is_and_andi));
  Multiplexer #(.enable("false"), .width(4)) multiplexer_18 (
    .in0(4'b0000), .in1(R_I_ALUSel), .out(multiplexer_18_out), .sel(or_12_out));
  Multiplexer #(.enable("false"), .width(4)) multiplexer_19 (
    .in0(4'b0000), .in1(4'b1101), .out(multiplexer_19_out), .sel(is_lui));
  or or_13 (is_srl_srli, is_srl, is_srli);
  or or_14 (is_sra_srai, is_sra, is_srai);
  or or_15 (is_or_ori, is_or, is_ori);
  or or_16 (is_and_andi, is_and, is_andi);
  assign ALUSel = multiplexer_18_out | multiplexer_19_out;  // OR_Gate or_17, 4 bits wide
  assign R_I_ALUSel = multiplexer_6_out | multiplexer_7_out | multiplexer_8_out | multiplexer_9_out | multiplexer_10_out | multiplexer_11_out | multiplexer_12_out | multiplexer_13_out | multiplexer_14_out | multiplexer_15_out | multiplexer_16_out | multiplexer_17_out;  // OR_Gate or_18, 4 bits wide
  Comparator #(.width(3)) comparator_39 (.a(inst[14:12]), .b(3'b001), .eq(comparator_39_eq));  // open: gt, lt
  Comparator #(.width(3)) comparator_40 (.a(inst[14:12]), .b(3'b101), .eq(comparator_40_eq));  // open: gt, lt
  and and_37 (is_csrw, comparator_39_eq, CSRWen);
  and and_38 (CSRSel, comparator_40_eq, CSRWen);
  or or_19 (or_19_out, is_R, is_I_imm, is_auipc, is_lui);
  or or_20 (or_20_out, is_jal, is_jalr);
  Multiplexer #(.enable("false"), .width(2)) multiplexer_20 (
    .in0(2'b00), .in1(2'b01), .out(multiplexer_20_out), .sel(or_19_out));
  Multiplexer #(.enable("false"), .width(2)) multiplexer_21 (
    .in0(2'b00), .in1(2'b10), .out(multiplexer_21_out), .sel(or_20_out));
  assign WBSel = multiplexer_20_out | multiplexer_21_out;  // OR_Gate or_21, 2 bits wide

  // Other names for the same wires on the sheet: funct7[6:0] = inst[31:25]; funct3[2:0] = inst[14:12];
  //   opcode[6:0] = inst[6:0]; rd[4:0] = inst[11:7]; rs1[4:0] = inst[19:15]; rs2[4:0] = inst[24:20]; is_csr = CSRWen;
  //   is_csrwi = CSRSel; is_S = MemRW

  // Notes on the sheet:
  //   INPUTS to your circuit
  //   DON'T CHANGE THE LOCATIONS OF THE INPUTS AND OUTPUTS!
  //   OUTPUT from your circuit
endmodule
