// Logisim project cpu.circ as structural Verilog: 2 circuits, main circuit cpu
module cpu (
  input  clk,
  input  [31:0] INSTRUCTION,
  input  [31:0] READ_DATA,
  output [31:0] WRITE_ADDRESS,
  output [31:0] PROGRAM_COUNTER,
  output [31:0] ra,
  output [31:0] sp,
  output [31:0] t0,
  output [31:0] t1,
  output [31:0] t2,
  output [31:0] s0,
  output [31:0] s1,
  output [31:0] a0,
  output [31:0] tohost,
  output [3:0] WRITE_ENABLE,
  output [31:0] WRITE_DATA
);

  wire ASel, BrEq, BrLT, BrUn, BSel, CSRSel, CSRWen, flush, MemRW, register_3_q, RegWEn;
  wire [1:0] WBSel;
  wire [2:0] EX_FUNCT3, ImmSel;
  wire [3:0] ALUSel;
  wire [11:0] csr_src, register_4_q;
  wire [19:0] EX_INST;
  wire [31:0] adder_1_out, adder_2_out, bit_extender_1_out, EX_PC, gen_imm, multiplexer_1_out,
       multiplexer_2_out, multiplexer_3_out, multiplexer_4_out, multiplexer_5_out, Rdata1, WBdata;

  Adder #(.width(32)) adder_1 (.a(PROGRAM_COUNTER), .b(32'h4), .out(adder_1_out));  // open: cin, cout
  Multiplexer #(.enable("false"), .width(32)) multiplexer_1 (
    .in0(adder_1_out), .in1(WRITE_ADDRESS), .out(multiplexer_1_out), .sel(flush));
  Register #(.width(32)) PC (.D(multiplexer_1_out), .clk(clk), .Q(PROGRAM_COUNTER));  // open: en, clr
  Multiplexer #(.enable("false"), .width(32)) multiplexer_2 (
    .in0(INSTRUCTION), .in1(32'h13), .out(multiplexer_2_out), .sel(flush));
  Register #(.width(32)) register_1 (
    .D(multiplexer_2_out), .clk(clk), .Q({csr_src, EX_INST[19:15], EX_FUNCT3, EX_INST[11:0]}));  // open: en, clr
  control_logic control_logic_1 (
    .CSRWen(CSRWen), .PCSel(flush), .RegWEn(RegWEn), .ImmSel(ImmSel), .BrUn(BrUn), .ASel(ASel), .BSel(BSel),
    .ALUSel(ALUSel), .MemRW(MemRW), .WBSel(WBSel), .CSRSel(CSRSel),
    .inst({csr_src, EX_INST[19:15], EX_FUNCT3, EX_INST[11:0]}), .BrEq(BrEq), .BrLt(BrLT));
  Register #(.width(32)) register_2 (.D(PROGRAM_COUNTER), .clk(clk), .Q(EX_PC));  // open: en, clr
  imm_gen imm_gen_1 (.inst({csr_src, EX_INST[19:15], EX_FUNCT3, EX_INST[11:0]}), .ImmSel(ImmSel), .imm(gen_imm));
  regfile regfile_1 (
    .rs1(EX_INST[19:15]), .rs2(csr_src[4:0]), .rd(EX_INST[11:7]), .Write_Data(WBdata), .RegWEn(RegWEn),
    .clk(clk), .ra(ra), .sp(sp), .t0(t0), .t1(t1), .t2(t2), .s0(s0), .s1(s1), .a0(a0), .Read_Data_1(Rdata1),
    .Read_Data_2(WRITE_DATA));
  Multiplexer #(.enable("false"), .width(32)) multiplexer_3 (
    .in0(Rdata1), .in1(EX_PC), .out(multiplexer_3_out), .sel(ASel));
  Multiplexer #(.enable("false"), .width(32)) multiplexer_4 (
    .in0(WRITE_DATA), .in1(gen_imm), .out(multiplexer_4_out), .sel(BSel));
  assign bit_extender_1_out = {{27{EX_INST[19]}}, EX_INST[19:15]};  // Bit_Extender bit_extender_1
  Register #(.width(1)) register_3 (.D(CSRWen), .clk(clk), .Q(register_3_q));  // open: en, clr
  Register #(.width(12)) register_4 (.D(csr_src), .clk(clk), .Q(register_4_q));  // open: en, clr
  Multiplexer #(.enable("false"), .width(32)) multiplexer_5 (
    .in0(Rdata1), .in1(bit_extender_1_out), .out(multiplexer_5_out), .sel(CSRSel));
  alu alu_1 (.Result(WRITE_ADDRESS), .A(multiplexer_3_out), .B(multiplexer_4_out), .ALUSel(ALUSel));
  branch_comp branch_comp_1 (.rs1(Rdata1), .rs2(WRITE_DATA), .BrUn(BrUn), .BrEq(BrEq), .BrLt(BrLT));
  Adder #(.width(32)) adder_2 (.a(EX_PC), .b(32'h4), .out(adder_2_out));  // open: cin, cout
  csr csr_1 (
    .CSR_address(register_4_q), .CSR_din(multiplexer_5_out), .CSR_WE(register_3_q), .clk(clk), .tohost(tohost));
  Multiplexer #(.enable("false"), .select(2), .width(32)) multiplexer_6 (
    .in0(READ_DATA), .in1(WRITE_ADDRESS), .in2(adder_2_out), .out(WBdata), .sel(WBSel));  // open: in3
  mem_pre mem_pre_1 (.address(WRITE_ADDRESS), .memRW(MemRW), .func3(EX_FUNCT3), .Write_En(WRITE_ENABLE));

  // Other names for the same wires on the sheet: ALUres[31:0] = WRITE_ADDRESS;
  //   EX_INST (some bits) = {csr_src, EX_FUNCT3}; rs1[4:0] = EX_INST[19:15]; PCsel = flush; Rdata2[31:0] = WRITE_DATA

  // Notes on the sheet:
  //   Output to IMEM
  //   IMEM (do **NOT** move this)
  //   Inputs from IMEM
  //   It is OK to move the PC, RegFile, ALU, MEM, Branch Comp, Imm Gen, and Control Logic to wherever is most convenient for you when constructing your CPU, and to delete this text
  //   Inputs/Outputs for testing. Do **NOT** move these.
  //   Outputs To DMEM
  //   DMEM (do **NOT** move this)
  //   Inputs From DMEM
endmodule

module mem_pre (
  input  [31:0] address,
  input  memRW,
  input  [2:0] func3,
  output [3:0] Write_En
);

  wire and_1_out, and_2_out, is_b, is_h, is_w, not_1_out;
  wire [3:0] multiplexer_1_out, multiplexer_2_out, multiplexer_3_out, multiplexer_4_out, multiplexer_5_out,
       or_1_out;

  Comparator #(.mode("unsigned"), .width(3)) comparator_1 (.a(func3), .b(3'b000), .eq(is_b));  // open: gt, lt
  Comparator #(.mode("unsigned"), .width(3)) comparator_2 (.a(func3), .b(3'b001), .eq(is_h));  // open: gt, lt
  Comparator #(.mode("unsigned"), .width(3)) comparator_3 (.a(func3), .b(3'b010), .eq(is_w));  // open: gt, lt
  and and_1 (and_1_out, is_h, not_1_out);
  not not_1 (not_1_out, address[1]);
  and and_2 (and_2_out, is_h, address[1]);
  Multiplexer #(.enable("false"), .select(2), .width(4)) multiplexer_1 (
    .in0(4'b0001), .in1(4'b0010), .in2(4'b0100), .in3(4'b1000), .out(multiplexer_1_out), .sel(address[1:0]));
  Multiplexer #(.enable("false"), .width(4)) multiplexer_2 (
    .in0(4'b0000), .in1(4'b1111), .out(multiplexer_2_out), .sel(is_w));
  Multiplexer #(.enable("false"), .width(4)) multiplexer_3 (
    .in0(4'b0000), .in1(4'b0011), .out(multiplexer_3_out), .sel(and_1_out));
  Multiplexer #(.enable("false"), .width(4)) multiplexer_4 (
    .in0(4'b0000), .in1(4'b1100), .out(multiplexer_4_out), .sel(and_2_out));
  Multiplexer #(.enable("false"), .width(4)) multiplexer_5 (
    .in0(4'b0000), .in1(multiplexer_1_out), .out(multiplexer_5_out), .sel(is_b));
  Multiplexer #(.enable("false"), .width(4)) multiplexer_6 (.in0(4'b0000), .in1(or_1_out), .out(Write_En), .sel(memRW));
  assign or_1_out = multiplexer_2_out | multiplexer_3_out | multiplexer_4_out | multiplexer_5_out;  // OR_Gate or_1, 4 bits wide

  // Other names for the same wires on the sheet: addr01[1:0] = address[1:0]; addr1 = address[1]; funct3[2:0] = func3
endmodule
