// Logisim project regfile.circ as structural Verilog: 1 circuit, main circuit regfile
module regfile (
  input  [4:0] rs1,
  input  [4:0] rs2,
  input  [4:0] rd,
  input  [31:0] Write_Data,
  input  RegWEn,
  input  clk,
  output [31:0] ra,
  output [31:0] sp,
  output [31:0] t0,
  output [31:0] t1,
  output [31:0] t2,
  output [31:0] s0,
  output [31:0] s1,
  output [31:0] a0,
  output [31:0] Read_Data_1,
  output [31:0] Read_Data_2
);

  wire x0WE, x1WE, x2WE, x3WE, x4WE, x5WE, x6WE, x7WE, x8WE, x9WE, x10WE, x11WE, x12WE, x13WE, x14WE, x15WE,
       x16WE, x17WE, x18WE, x19WE, x20WE, x21WE, x22WE, x23WE, x24WE, x25WE, x26WE, x27WE, x28WE, x29WE,
       x30WE, x31WE;
  wire [31:0] x0out, x3out, x4out, x11out, x12out, x13out, x14out, x15out, x16out, x17out, x18out, x19out,
       x20out, x21out, x22out, x23out, x24out, x25out, x26out, x27out, x28out, x29out, x30out, x31out;

  Register #(.width(32)) register_1 (.D({32{1'b0}}), .en(x0WE), .clk(clk), .Q(x0out));  // open: clr
  Register #(.width(32)) register_2 (.D(Write_Data), .en(x4WE), .clk(clk), .Q(x4out));  // open: clr
  Register #(.width(32)) register_3 (.D(Write_Data), .en(x8WE), .clk(clk), .Q(s0));  // open: clr
  Register #(.width(32)) register_4 (.D(Write_Data), .en(x12WE), .clk(clk), .Q(x12out));  // open: clr
  Register #(.width(32)) register_5 (.D(Write_Data), .en(x16WE), .clk(clk), .Q(x16out));  // open: clr
  Register #(.width(32)) register_6 (.D(Write_Data), .en(x20WE), .clk(clk), .Q(x20out));  // open: clr
  Register #(.width(32)) register_7 (.D(Write_Data), .en(x24WE), .clk(clk), .Q(x24out));  // open: clr
  Register #(.width(32)) register_8 (.D(Write_Data), .en(x28WE), .clk(clk), .Q(x28out));  // open: clr
  Multiplexer #(.enable("false"), .select(5), .width(32)) multiplexer_1 (
    .in0(x0out), .in1(ra), .in2(sp), .in3(x3out), .in4(x4out), .in5(t0), .in6(t1), .in7(t2), .in8(s0),
    .in9(s1), .in10(a0), .in11(x11out), .in12(x12out), .in13(x13out), .in14(x14out), .in15(x15out),
    .in16(x16out), .in17(x17out), .in18(x18out), .in19(x19out), .in20(x20out), .in21(x21out), .in22(x22out),
    .in23(x23out), .in24(x24out), .in25(x25out), .in26(x26out), .in27(x27out), .in28(x28out), .in29(x29out),
    .in30(x30out), .in31(x31out), .out(Read_Data_1), .sel(rs1));
  Register #(.width(32)) register_9 (.D(Write_Data), .en(x1WE), .clk(clk), .Q(ra));  // open: clr
  Register #(.width(32)) register_10 (.D(Write_Data), .en(x5WE), .clk(clk), .Q(t0));  // open: clr
  Register #(.width(32)) register_11 (.D(Write_Data), .en(x9WE), .clk(clk), .Q(s1));  // open: clr
  Register #(.width(32)) register_12 (.D(Write_Data), .en(x13WE), .clk(clk), .Q(x13out));  // open: clr
  Register #(.width(32)) register_13 (.D(Write_Data), .en(x17WE), .clk(clk), .Q(x17out));  // open: clr
  Register #(.width(32)) register_14 (.D(Write_Data), .en(x21WE), .clk(clk), .Q(x21out));  // open: clr
  Register #(.width(32)) register_15 (.D(Write_Data), .en(x25WE), .clk(clk), .Q(x25out));  // open: clr
  Register #(.width(32)) register_16 (.D(Write_Data), .en(x29WE), .clk(clk), .Q(x29out));  // open: clr
  Register #(.width(32)) register_17 (.D(Write_Data), .en(x2WE), .clk(clk), .Q(sp));  // open: clr
  Register #(.width(32)) register_18 (.D(Write_Data), .en(x6WE), .clk(clk), .Q(t1));  // open: clr
  Register #(.width(32)) register_19 (.D(Write_Data), .en(x10WE), .clk(clk), .Q(a0));  // open: clr
  Register #(.width(32)) register_20 (.D(Write_Data), .en(x14WE), .clk(clk), .Q(x14out));  // open: clr
  Register #(.width(32)) register_21 (.D(Write_Data), .en(x18WE), .clk(clk), .Q(x18out));  // open: clr
  Register #(.width(32)) register_22 (.D(Write_Data), .en(x22WE), .clk(clk), .Q(x22out));  // open: clr
  Register #(.width(32)) register_23 (.D(Write_Data), .en(x26WE), .clk(clk), .Q(x26out));  // open: clr
  Register #(.width(32)) register_24 (.D(Write_Data), .en(x30WE), .clk(clk), .Q(x30out));  // open: clr
  Multiplexer #(.enable("false"), .select(5), .width(32)) multiplexer_2 (
    .in0(x0out), .in1(ra), .in2(sp), .in3(x3out), .in4(x4out), .in5(t0), .in6(t1), .in7(t2), .in8(s0),
    .in9(s1), .in10(a0), .in11(x11out), .in12(x12out), .in13(x13out), .in14(x14out), .in15(x15out),
    .in16(x16out), .in17(x17out), .in18(x18out), .in19(x19out), .in20(x20out), .in21(x21out), .in22(x22out),
    .in23(x23out), .in24(x24out), .in25(x25out), .in26(x26out), .in27(x27out), .in28(x28out), .in29(x29out),
    .in30(x30out), .in31(x31out), .out(Read_Data_2), .sel(rs2));
  Register #(.width(32)) register_25 (.D(Write_Data), .en(x3WE), .clk(clk), .Q(x3out));  // open: clr
  Register #(.width(32)) register_26 (.D(Write_Data), .en(x7WE), .clk(clk), .Q(t2));  // open: clr
  Register #(.width(32)) register_27 (.D(Write_Data), .en(x11WE), .clk(clk), .Q(x11out));  // open: clr
  Register #(.width(32)) register_28 (.D(Write_Data), .en(x15WE), .clk(clk), .Q(x15out));  // open: clr
  Register #(.width(32)) register_29 (.D(Write_Data), .en(x19WE), .clk(clk), .Q(x19out));  // open: clr
  Register #(.width(32)) register_30 (.D(Write_Data), .en(x23WE), .clk(clk), .Q(x23out));  // open: clr
  Register #(.width(32)) register_31 (.D(Write_Data), .en(x27WE), .clk(clk), .Q(x27out));  // open: clr
  Register #(.width(32)) register_32 (.D(Write_Data), .en(x31WE), .clk(clk), .Q(x31out));  // open: clr
  Decoder #(.select(5)) decoder_1 (
    .out0(x0WE), .out1(x1WE), .out2(x2WE), .out3(x3WE), .out4(x4WE), .out5(x5WE), .out6(x6WE), .out7(x7WE),
    .out8(x8WE), .out9(x9WE), .out10(x10WE), .out11(x11WE), .out12(x12WE), .out13(x13WE), .out14(x14WE),
    .out15(x15WE), .out16(x16WE), .out17(x17WE), .out18(x18WE), .out19(x19WE), .out20(x20WE), .out21(x21WE),
    .out22(x22WE), .out23(x23WE), .out24(x24WE), .out25(x25WE), .out26(x26WE), .out27(x27WE), .out28(x28WE),
    .out29(x29WE), .out30(x30WE), .out31(x31WE), .sel(rd), .en(RegWEn));

  // Other names for the same wires on the sheet: read_data1[31:0] = Read_Data_1; read_data2[31:0] = Read_Data_2;
  //   read_reg1[4:0] = rs1; read_reg2[4:0] = rs2; write_en = RegWEn; write_reg[4:0] = rd; x1out[31:0] = ra;
  //   x2out[31:0] = sp; x5out[31:0] = t0; x6out[31:0] = t1; x7out[31:0] = t2; x8out[31:0] = s0; x9out[31:0] = s1;
  //   x10out[31:0] = a0

  // Notes on the sheet:
  //   INPUTS to your circuit
  //   DON'T CHANGE THE LOCATIONS OF THE INPUTS AND OUTPUTS!
  //   These are DEBUG/TEST outputs from your circuit.
  //   OUTPUTS from your circuit
endmodule
